# Fritzing sketch schema (saved by Fritzing 0.9.3b)

parts:
  U1 = NodeMCU V3.0
  VCC1 = Battery
  U2 = mystery part, 6 pins [part_number="backup battery module" chip_label=?]
  HLK-PM1 = HLK-PM01
  Mod1 = zmpt101b
  J3 = screw terminal, 2 pins
  RHT1 = Humidity and Temperature Sensor RHT03
  LED3 = LED - 5mm [color="Blue (470nm)" package="5 mm [THT]"]
  R1 = Resistor [tolerance=±5% resistance=100 package=THT]

nets:
  N1: U1.D1, RHT1.Data-signal
  LED: U1.D4, LED3.anode
  3.3V: U1.3V3, Mod1.VCC, RHT1.Vcc
  GND: U1.GND, U2.pin6, Mod1.GND, RHT1.GND_2, R1.Pin_0
  OUT+: U1.Vin, U2.pin5
  N2: U1.A0, Mod1.OUT
  N3: VCC1.-, U2.pin3
  N4: VCC1.+, U2.pin4
  N5: U2.pin1, HLK-PM1.-Vo
  N6: U2.pin2, HLK-PM1.+Vo
  N7: HLK-PM1.AC#0, Mod1.N, J3.pin1
  N8: HLK-PM1.AC#1, Mod1.L, J3.pin2
  N9: LED3.cathode, R1.Pin_1

notes:
  ESP8266Tempurature, sirapol nokyoongtong

custom parts:
  NodeMCU V3.0: ESP8266 based NodeMCU
  Battery: Your standard 2x 18650 battery pack (7,4 Volts)
  HLK-PM01: AC-DC 220V to 5V Step-Down Power Supply Module
  zmpt101b: Single phase ac active output voltate transformer module.
